# Fritzing sketch Amplified Theremin (saved by Fritzing 0.8.0b)
breadboards: 1

parts:
  Part1 = Arduino Uno (Rev3)
  SPKR1 = Loudspeaker
  S1 = Pushbutton [package="[THT]"]
  Q1 = NPN-Transistor [package="TO92 [THT]"]
  R1 = Photocell (LDR) [package=THT]
  R2 = Resistor [tolerance=±5% resistance=220 package=THT]

nets:
  N1: Part1.A0, R1.pin_0, R2.Pin_1
  N2: Part1.GND, S1.Pin_1, S1.Pin_2, R1.pin_1
  N3: Part1.D9_PWM, Q1.B
  N4: Part1.5V, R2.Pin_0
  N5: SPKR1.pin1, Q1.E
  N6: S1.Pin_3, S1.Pin_4, Q1.C
