# Fritzing sketch Potentiometer (saved by Fritzing 0.7.12b)
breadboards: 1

parts:
  Arduino1 = Arduino
  R1 = Rotary Potentiometer (Small) [maximum_resistance=100kΩ]
  S1 = Pushbutton [package="[THT]"]
  SPKR1 = Loudspeaker

nets:
  N1: Arduino1.GND, R1.leg2, S1.Pin_1, S1.Pin_2
  N2: Arduino1.D9, SPKR1.pin1
  N3: Arduino1.+5V, R1.leg1
  N4: Arduino1.A0, R1.wiper
  N5: S1.Pin_3, S1.Pin_4, SPKR1.pin2
