# Fritzing sketch Theremin (saved by Fritzing 0.8.0b)
breadboards: 1

parts:
  Arduino1 = Arduino
  R1 = Photocell (LDR) [package=THT]
  R2 = Resistor [tolerance=±5% resistance=10k package=THT]
  S1 = Pushbutton [package="[THT]"]
  SPKR1 = Loudspeaker

nets:
  N1: Arduino1.D9, SPKR1.pin2
  N2: Arduino1.+5V, R1.pin_0
  N3: Arduino1.GND, R2.Pin_1, S1.Pin_3, S1.Pin_4
  N4: Arduino1.A0, R1.pin_1, R2.Pin_0
  N5: S1.Pin_1, S1.Pin_2, SPKR1.pin1
